// Logisim project ULA IC.circ as structural Verilog: 6 circuits, main circuit Somador Completo
module Somador_Completo (
  input  A1,
  input  B1,
  input  A2,
  input  B2,
  output out_5,
  output out_6,
  output out_7,
  output out_8
);

  wire and_1_out, and_2_out, and_3_out, and_4_out, and_5_out, and_6_out, xor_1_out, xor_3_out;

  ExactlyOne xor_1 (.out(xor_1_out), .in0(A2), .in1(B2), .in2(out_5));
  and and_1 (and_1_out, out_5, A2);
  and and_2 (and_2_out, out_5, B2);
  and and_3 (and_3_out, B2, A2);
  xor xor_2 (out_7, xor_1_out, out_5);
  or or_1 (out_6, and_1_out, and_2_out, and_3_out);
  ExactlyOne xor_3 (.out(xor_3_out), .in0(A1), .in1(B1), .in2(1'b0));
  and and_4 (and_4_out, 1'b0, A1);
  and and_5 (and_5_out, 1'b0, B1);
  and and_6 (and_6_out, B1, A1);
  xor xor_4 (out_8, xor_3_out, 1'b0);
  or or_2 (out_5, and_4_out, and_5_out, and_6_out);
endmodule

module ALU_2Bits (
);

  Somador_Completo somador_completo ();  // open: A2, B2, out_5, A1, B1, out_6, out_7, out_8
  MUX_4x1 mux_4x1_1 ();  // open: in_1, in_2, in_3, in_4, in_5, in_6, out_7
  Subtrador_Completo subtrador_completo ();  // open: A1_2, B1_2, out_5, A1, B1, out_6, out_7, out_8
  Divider divider_1 ();  // open: a, b, out, upper, rem
  multiplier_2bits multiplier_2bits_1 ();  // open: A1, A2, B1, B2, R1, R2, R3, R4
endmodule

module Subtrador_Completo (
  input  A1,
  input  B1,
  input  A1_2,
  input  B1_2,
  output out_5,
  output out_6,
  output out_7,
  output out_8
);

  wire and_1_out, and_2_out, and_3_out, and_4_out, and_5_out, and_6_out, not_1_out, not_2_out, not_3_out,
       not_4_out, xor_1_out, xor_3_out;

  not not_1 (not_1_out, A1_2);
  not not_2 (not_2_out, A1_2);
  xor xor_1 (xor_1_out, A1_2, B1_2);
  and and_1 (and_1_out, not_1_out, B1_2);
  and and_2 (and_2_out, not_2_out, out_5);
  and and_3 (and_3_out, B1_2, out_5);
  xor xor_2 (out_7, xor_1_out, out_5);
  or or_1 (out_6, and_1_out, and_2_out, and_3_out);
  not not_3 (not_3_out, A1);
  not not_4 (not_4_out, A1);
  xor xor_3 (xor_3_out, A1, B1);
  and and_4 (and_4_out, not_3_out, B1);
  and and_5 (and_5_out, not_4_out, 1'b0);
  and and_6 (and_6_out, B1, 1'b0);
  xor xor_4 (out_8, xor_3_out, 1'b0);
  or or_2 (out_5, and_4_out, and_5_out, and_6_out);
endmodule

module MUX_4x1 (
  input  in_1,
  input  in_2,
  input  in_3,
  input  in_4,
  input  in_5,
  input  in_6,
  output out_7
);

  wire and_1_out, and_2_out, and_3_out, and_4_out, and_5_out, and_6_out, and_7_out, and_8_out, not_1_out,
       not_2_out, not_3_out, not_4_out;

  not not_1 (not_1_out, in_5);
  not not_2 (not_2_out, in_6);
  not not_3 (not_3_out, in_5);
  not not_4 (not_4_out, in_6);
  and and_1 (and_1_out, not_1_out, not_2_out);
  and and_2 (and_2_out, not_3_out, in_6);
  and and_3 (and_3_out, in_5, not_4_out);
  and and_4 (and_4_out, in_5, in_6);
  and and_5 (and_5_out, in_1, and_1_out);
  and and_6 (and_6_out, in_2, and_2_out);
  and and_7 (and_7_out, in_3, and_3_out);
  and and_8 (and_8_out, in_4, and_4_out);
  or or_1 (out_7, and_5_out, and_6_out, and_7_out, and_8_out);
endmodule

// multiplier
module multiplier_2bits (
  input  A1,
  input  A2,
  input  B1,
  input  B2,
  output R1,
  output R2,
  output R3,
  output R4
);

  wire and_2_out, and_3_out, and_4_out, and_5_out, and_6_out, and_7_out, not_1_out, not_2_out, not_3_out,
       not_4_out, not_5_out, not_6_out;

  and and_1 (R1, A1, A2, B1, B2);
  not not_1 (not_1_out, A2);
  and and_2 (and_2_out, A1, not_1_out, B1);
  and and_3 (and_3_out, A1, B1, not_2_out);
  not not_2 (not_2_out, B2);
  not not_3 (not_3_out, A1);
  and and_4 (and_4_out, not_3_out, A2, B1);
  and and_5 (and_5_out, A2, B1, not_4_out);
  not not_4 (not_4_out, B2);
  and and_6 (and_6_out, A1, not_5_out, B2);
  not not_5 (not_5_out, A2);
  and and_7 (and_7_out, A1, not_6_out, B2);
  not not_6 (not_6_out, B1);
  and and_8 (R4, A2, B2);
  or or_1 (R2, and_2_out, and_3_out);
  or or_2 (R3, and_4_out, and_5_out, and_6_out, and_7_out);
endmodule

module divisor (
);

  Divider #(.width(2)) divider_1 ();  // open: a, b, out, upper, rem
endmodule
